# Fritzing sketch sketch (saved by Fritzing 0.9.0b)
breadboards: 1

parts:
  CC3K1 = Adafruit CC3000 WiFi Breakout
  Part1 = Arduino Uno (Rev3)
  R1 = Resistor [package="2512 [SMD]"]
  LED1 = LED - 3mm [color="Red (633nm)" package="3 mm [THT]"]

nets:
  GND: CC3K1.GND, Part1.GND, LED1.cathode
  VIN: CC3K1.VIN, Part1.5V
  N1: CC3K1.CLK, Part1.D13/SCK
  N2: CC3K1.MISO, Part1.D12/MISO
  N3: CC3K1.MOSI, Part1.D11_PWM/MOSI
  N4: CC3K1.CS, Part1.D10_PWM/SS
  N5: CC3K1.VBEN, Part1.D5_PWM
  N6: CC3K1.IRQ, Part1.D3_PWM
  N7: CC3K1.TXD, CC3K1.RXD
  N8: Part1.D7, R1.Pin_1
  N9: R1.Pin_0, LED1.anode

custom parts:
  Adafruit CC3000 WiFi Breakout: CC3000 WiFi Breakout
